# Fritzing sketch Greenhouse (saved by Fritzing 1.0.1rc)
breadboards: 2

parts:
  Mod1 = KY-026 Flame Sensor Module [package="Breakout board"]
  LED1 = LED - 5mm [color="Red (633nm)" current=0.030 package="5 mm [THT]"]
  LED2 = LED - 5mm [color="White (8000K)" current=0.030 package="5 mm [THT]"]
  DHT1 = DHT11 Humitidy and Temperature Sensor
  Mod2 = KY-018 Photoresistor Module [package="Breakout board"]
  Mod3 = KY-012 Active Buzzer Module [package="Breakout board"]
  J1 = Basic Servo
  LCM1602_IIC1 = LCM1602 IIC [part_number="LCM1602 IIC" chip_label="LCM1602 IIC" package="DIP (Dual Inline) [THT]"]
  U1 = ESP8266 NodeMCU LoLin module
  R1 = Resistor [tolerance=±5% resistance=100 package="2010 [SMD]"]
  R2 = Resistor [tolerance=±5% resistance=220 package="2010 [SMD]"]
  R3 = Resistor [tolerance=±5% resistance=220 package="2010 [SMD]"]
  S1 = Pushbutton [package="[THT]"]
  R4 = Resistor [tolerance=±5% power=0.25 resistance=10k package=THT]

nets:
  GND: Mod1.G, DHT1.GND, Mod2.-, J1.gnd, LCM1602_IIC1.GND, U1.GND, S1.Pin_3, S1.Pin_4
  VDD: Mod1.+, DHT1.VDD, Mod2.Vin, U1.3V3, R1.Pin_0, R2.Pin_1, R3.Pin_1, R4.Pin_1
  N1: Mod1.D0, U1.D5
  N2: LED1.cathode, Mod3.-, U1.D4
  N3: LED1.anode, R2.Pin_0
  N4: LED2.cathode, U1.D0
  N5: LED2.anode, R3.Pin_0
  N6: DHT1.DATA, U1.D7
  N7: Mod2.S, U1.A0
  N8: Mod3.S, R1.Pin_1
  VCC: J1.vcc, LCM1602_IIC1.VCC, U1.Vin
  N9: J1.pulse, U1.D6
  N10: LCM1602_IIC1.SDA, U1.D2
  N11: LCM1602_IIC1.SCL, U1.D1
  N12: U1.D3, S1.Pin_1, S1.Pin_2, R4.Pin_0

notes:
  Attenzione a pin D3 perche è per la FLASH
  D4 deve essere High all'avvio

custom parts:
  KY-026 Flame Sensor Module: KY-026 Flame Sensor Module reacts in the presence of fire.
  DHT11 Humitidy and Temperature Sensor: DHT11 Humidity and Temperature Sensor
  KY-018 Photoresistor Module: KY-018 Photoresistor module, used to measure light intensity. It can determine the presence or absence of light.
  KY-012 Active Buzzer Module: Active Piezoelectric Buzzer Module KY-012, it produces single-tone sound when signal is high. (Special thanks to vanepp for fixing the PCB holes and other errors)
  LCM1602 IIC: I2C-Module to use a 1602 or 2004 LCD on with the wire.h libory Serial LCD Modul
  ESP8266 NodeMCU LoLin module: ESP8266 based NodeMCU
